# Fritzing sketch sketch (saved by Fritzing 0.9.4)
breadboards: 1

parts:
  NorthWest_ID_1 = Vibration Motor- ROB-08449 [package=vibe-motor-10mm]
  NorthEast_ID_3 = Vibration Motor- ROB-08449 [package=vibe-motor-10mm]
  Q1 = NPN-Transistor [package="TO92 [THT]"]
  Q2 = NPN-Transistor [package="TO92 [THT]"]
  Raspberry_Pi_1 = Raspberry Pi 3 [part_number=RPI-3-V1.2]
  Q3 = NPN-Transistor [package="TO92 [THT]"]  # not connected

nets:
  N1: NorthWest_ID_1.+, Q1.B
  N2: NorthWest_ID_1.-, NorthEast_ID_3.-, Raspberry_Pi_1.3v3
  N3: NorthEast_ID_3.+, Q2.B
  N4: Q1.E, Q2.E, Raspberry_Pi_1.GND
  N5: Q1.C, Raspberry_Pi_1.GIPO18
  N6: Q2.C, Raspberry_Pi_1.GIPO22

notes:
  GPIO 1
  GPIO 3
  Emitter
  Collector
  Base
